// Logisim project GEO_SAP1_v7.circ as structural Verilog: 1 circuit, main circuit main
module main (
  input  _1___AUTO
);

  wire adder_1_cout, and_1_out, and_2_out, and_5_out, and_6_out, and_7_out, and_8_out, and_9_out, and_10_out,
       and_11_out, and_12_out, and_13_out, and_14_out, button_1_out, button_2_out, button_3_out, CE,
       clock_1_out, CP, CPd, EA, Ei, EP, EU, HLT, LA, LB, Li, LM, LO, nand_1_out, nand_2_out, nand_3_out,
       nand_4_out, nand_5_out, nand_6_out, nand_7_out, nand_8_out, nand_9_out, nand_10_out, nand_11_out,
       nand_12_out, nand_13_out, nand_14_out, nand_15_out, nand_16_out, nand_17_out, nand_18_out, nor_1_out,
       not_1_out, not_2_out, not_4_out, or_1_out, or_2_out, or_4_out, shift_register_1_out,
       shift_register_1_q2, shift_register_1_q3, shift_register_1_q4, shift_register_1_q5, SU, WM;
  wire [3:0] controlled_buffer_1_out, controlled_buffer_3_out, controlled_buffer_4_out, counter_1_q,
       ram_1_data, register_1_q, register_2_q, register_2_q_2, xor_1_out, xor_5_out;
  wire [7:0] adder_1_out, register_4_q, register_5_q, undriven;
  wire [7:4] register_3_q;

  Button button_1 (.out(button_1_out));
  Button button_2 (.out(button_2_out));
  or or_1 (or_1_out, button_2_out, and_1_out);
  nand nand_1 (nand_1_out, and_9_out, shift_register_1_q3);
  nand nand_2 (nand_2_out, and_10_out, shift_register_1_q3);
  or or_2 (or_2_out, EP, ~nand_1_out, ~nand_2_out, ~nand_3_out);  // OR_Gate
  and and_1 (and_1_out, _1___AUTO, HLT, clock_1_out);
  nand nand_3 (nand_3_out, and_11_out, shift_register_1_q3);
  or or_3 (LM, or_2_out, WM);
  Clock clock_1 (.out(clock_1_out));
  not not_1 (not_1_out, or_1_out);
  nand nand_4 (nand_4_out, and_9_out, shift_register_1_q4);
  nand nand_5 (nand_5_out, and_10_out, shift_register_1_q4);
  or or_4 (or_4_out, shift_register_1_q2, ~nand_4_out, ~nand_5_out, ~nand_7_out);  // OR_Gate
  or or_5 (CE, and_7_out, or_4_out);
  not not_2 (not_2_out, shift_register_1_q2);
  nand nand_6 (nand_6_out, and_9_out, shift_register_1_q3);
  nand nand_7 (nand_7_out, and_11_out, shift_register_1_q4);
  not not_3 (Li, not_2_out);
  Shift_Register #(.length(6), .trigger("falling")) shift_register_1 (
    .in(shift_register_1_out), .clk(or_1_out), .out(shift_register_1_out), .load(button_1_out), .d0(1'b1),
    .q0(EP), .d1(1'b0), .q1(CP), .d2(1'b0), .q2(shift_register_1_q2), .d3(1'b0), .q3(shift_register_1_q3),
    .d4(1'b0), .q4(shift_register_1_q4), .d5(1'b0), .q5(shift_register_1_q5));  // open: shift, clr
  nand nand_8 (nand_8_out, and_10_out, shift_register_1_q3);
  nand nand_9 (nand_9_out, and_11_out, shift_register_1_q3);
  or or_6 (Ei, ~nand_6_out, ~nand_8_out, ~nand_9_out);  // OR_Gate
  nand nand_10 (nand_10_out, and_10_out, shift_register_1_q5);
  nand nand_11 (nand_11_out, and_9_out, shift_register_1_q4);
  or or_7 (LA, ~nand_11_out, ~nand_10_out, ~nand_12_out);  // OR_Gate
  assign controlled_buffer_1_out = not_4_out ? controlled_buffer_4_out : 4'bz;  // Controlled_Buffer controlled_buffer_1
  not not_4 (not_4_out, WM);
  assign controlled_buffer_1_out = WM ? undriven[3:0] : 4'bz;  // Controlled_Buffer controlled_buffer_2
  and and_2 (and_2_out, and_12_out, shift_register_1_q3);
  nand nand_12 (nand_12_out, and_11_out, shift_register_1_q5);
  or or_8 (EA, WM, and_2_out);
  Hex_Digit_Display hex_digit_display_1 (.value(register_2_q_2), .dp(1'b1));
  Hex_Digit_Display hex_digit_display_2 (.value(register_2_q), .dp(1'b1));
  Register #(.width(4)) register_1 (
    .D(controlled_buffer_1_out), .en(LM), .Q(register_1_q), .clk(or_1_out), .clr(button_1_out));
  and and_3 (SU, and_11_out, shift_register_1_q5);
  nand nand_13 (nand_13_out, and_10_out, shift_register_1_q5);
  nand nand_14 (nand_14_out, and_11_out, shift_register_1_q5);
  nand nand_15 (nand_15_out, and_10_out, shift_register_1_q4);
  or or_9 (EU, ~nand_13_out, ~nand_14_out);  // OR_Gate
  Register register_2 (
    .D({ram_1_data, controlled_buffer_4_out}), .en(LO), .Q({register_2_q_2, register_2_q}), .clk(or_1_out),
    .clr(button_1_out));
  nand nand_16 (nand_16_out, CE, WM);
  assign controlled_buffer_3_out = CPd ? undriven[3:0] : 4'bz;  // Controlled_Buffer controlled_buffer_3
  assign controlled_buffer_4_out = EP ? counter_1_q : 4'bz;  // Controlled_Buffer controlled_buffer_4
  Counter #(.width(4), .max('hf), .ongoal("stay"), .trigger("falling")) counter_1 (
    .load(CPd), .D(controlled_buffer_3_out), .count(CP), .Q(counter_1_q), .clk(not_1_out), .clr(button_1_out));  // open: carry
  nand nand_17 (nand_17_out, and_11_out, shift_register_1_q4);
  nand nand_18 (nand_18_out, and_12_out, shift_register_1_q3);
  nor nor_1 (nor_1_out, ~nand_15_out, ~nand_17_out);  // NOR_Gate
  not not_5 (LB, nor_1_out);
  not not_6 (LO, nand_18_out);
  RAM #(.addrWidth(4), .bus("asynch")) ram_1 (
    .addr(register_1_q), .data({ram_1_data, controlled_buffer_4_out}), .sel(CE), .ld(nand_16_out),
    .clr(button_3_out));
  Button button_3 (.out(button_3_out));
  and and_4 (CPd, shift_register_1_q3, and_8_out);
  assign {ram_1_data, controlled_buffer_4_out} = EU ? adder_1_out : 8'bz;  // Controlled_Buffer controlled_buffer_5
  assign {ram_1_data, controlled_buffer_4_out} = Ei ? undriven : 8'bz;  // Controlled_Buffer controlled_buffer_6
  Register register_3 (
    .D({ram_1_data, controlled_buffer_4_out}), .en(Li), .Q({register_3_q, undriven[3:0]}), .clk(or_1_out),
    .clr(button_1_out));
  and and_5 (and_5_out, shift_register_1_q3, and_13_out);
  and and_6 (and_6_out, shift_register_1_q4, and_13_out);
  or or_10 (WM, and_5_out, and_6_out);
  Register register_4 (
    .D({ram_1_data, controlled_buffer_4_out}), .en(LA), .Q(register_4_q), .clk(or_1_out), .clr(button_1_out));
  assign {ram_1_data, controlled_buffer_4_out} = EA ? register_4_q : 8'bz;  // Controlled_Buffer controlled_buffer_7
  Register register_5 (
    .D({ram_1_data, controlled_buffer_4_out}), .en(LB), .Q(register_5_q), .clk(or_1_out), .clr(button_1_out));
  and and_7 (and_7_out, shift_register_1_q4, and_13_out);
  and and_8 (and_8_out, register_3_q[4], ~register_3_q[5], ~register_3_q[6], register_3_q[7]);  // AND_Gate
  and and_9 (and_9_out, ~register_3_q[4], ~register_3_q[5], ~register_3_q[6], ~register_3_q[7]);  // AND_Gate
  and and_10 (and_10_out, register_3_q[4], ~register_3_q[5], ~register_3_q[6], ~register_3_q[7]);  // AND_Gate
  and and_11 (and_11_out, ~register_3_q[4], ~register_3_q[6], register_3_q[5], ~register_3_q[7]);  // AND_Gate
  and and_12 (and_12_out, ~register_3_q[4], register_3_q[5], register_3_q[6], register_3_q[7]);  // AND_Gate
  and and_13 (and_13_out, ~register_3_q[4], ~register_3_q[5], register_3_q[6], register_3_q[7]);  // AND_Gate
  not not_7 (HLT, and_14_out);
  and and_14 (and_14_out, register_3_q[4], register_3_q[5], register_3_q[6], register_3_q[7]);
  Adder #(.width(4)) adder_1 (
    .a(xor_1_out), .b(register_4_q[3:0]), .out(adder_1_out[3:0]), .cin(SU), .cout(adder_1_cout));
  Adder #(.width(4)) adder_2 (
    .a(xor_5_out), .b(register_4_q[7:4]), .out(adder_1_out[7:4]), .cin(adder_1_cout));  // open: cout
  xor xor_1 (xor_1_out[0], register_5_q[0], SU);
  xor xor_2 (xor_1_out[1], register_5_q[1], SU);
  xor xor_3 (xor_1_out[2], register_5_q[2], SU);
  xor xor_4 (xor_1_out[3], register_5_q[3], SU);
  xor xor_5 (xor_5_out[0], register_5_q[4], SU);
  xor xor_6 (xor_5_out[1], register_5_q[5], SU);
  xor xor_7 (xor_5_out[2], register_5_q[6], SU);
  xor xor_8 (xor_5_out[3], register_5_q[7], SU);

  // Notes on the sheet:
  //   INSTRUÇÕES
  //   RESET
  //   CLR
  //   Clicar com botão direito na RAM
  //   Carregar arquivo de IMAGEM desejado
  //   Manter pressionado RESET até que
  //   o contador em anel reinicie
  //   PULSADOR
  //   Você pode programar a RAM clicando em EDITAR CONTEÚDO
  //   CLOCK
  //   Eng. Alex G. S. Miranda - Maio de 2026
  //   Projeto: SAP-1 (Malvino & Brown. Digital Computer Electronics, 1993 - Cap. 10)
  //   Acrescentei as instruções JMP com OP 9x e STO com OP cx onde x = endereço
  //   0 = MANUAL
  //   _CLK
  //   CLK
  //   UNIDADE DE CONTROLE
  //   CONTADOR EM ANEL
  //   SAÍDA DE DADOS
  //   REM
  //   RAM 16 X 8
  //   REG. SAÍDA
  //   BARRAMENTO
  //   CLR-MEM.
  //   CONT. PROG.
  //   ACUMULADOR
  //   REGIST. B
  //   REG. INSTRUÇÕES
  //   LSB
  //   MSB
  //   JMP
  //   LDA
  //   ADD
  //   SUB
  //   OUT
  //   STO
  //   HALT
  //   DECODIFICADOR DE INSTRUÇÕES
  //   UNIDADE LÓGICO-ARITMÉTICA
endmodule
